# Fritzing sketch Illumination-Via-Ethernet (saved by Fritzing 0.9.3b)
breadboards: 1

parts:
  RGB_Strip_LED1 = RGB Strip LED
  Q1 = MOSFET-NCHANNEL [package=to220v]
  Q2 = MOSFET-NCHANNEL [package=to220v]
  Q3 = MOSFET-NCHANNEL [package=to220v]
  Часть1 = Arduino Leonardo (Rev3b)  # not connected
  R1 = Resistor [tolerance=±5% resistance=10k package="2010 [SMD]"]
  R2 = Resistor [tolerance=±5% resistance=10k package="2010 [SMD]"]
  R3 = Resistor [tolerance=±5% resistance=10k package="2010 [SMD]"]
  KY-1 = Keyes Relay [package=THT]
  KY-2 = Keyes Relay [package=THT]
  Часть2 = Arduino Board Ethernet

nets:
  N1: RGB_Strip_LED1.Blue_Connect#5, Q3.D
  N2: RGB_Strip_LED1.Red_Connect#6, Q2.D
  N3: RGB_Strip_LED1.Green_Connect#7, Q1.D
  N4: Q1.G, R1.Pin_1
  N5: Q1.S, Q2.S, Q3.S
  N6: Q2.G, R2.Pin_1
  N7: Q3.G, R3.Pin_1
  N8: R1.Pin_0, Часть2.D5_PWM
  N9: R2.Pin_0, Часть2.D6_PWM
  N10: R3.Pin_0, Часть2.D3_PWM
  N11: KY-1.signal, Часть2.D4
  N12: KY-1.power, KY-2.power, Часть2.5V
  N13: KY-2.signal, Часть2.D2_PWM
  N14: KY-2.ground, Часть2.GND

custom parts:
  RGB Strip LED: A tri-color Strip LED with red, green and blue. Pin order: red - common cathode - blue - green
  Keyes Relay: The Keyes 5V relay module is suitable for SCM development, home appliance control. It uses a 5V~12V TIL control signal which can control DC / AC signal.
